# Fritzing sketch CameraLighting (saved by Fritzing 0.8.7b)
perfboards: 1

parts:
  R2 = Resistor [tolerance=±5% resistance=220 package=THT]
  R1 = Resistor [tolerance=±5% resistance=220 package=THT]
  R3 = Resistor [tolerance=±5% resistance=220 package=THT]
  R4 = Resistor [tolerance=±5% resistance=360 package=THT]
  J1 = female pin header, 3 pins [form="♀ (female)"]
  LED2 = LED - 5mm [color="White (6500K)" package="5 mm [THT]"]
  LED3 = LED - 5mm [color="White (6500K)" package="5 mm [THT]"]
  LED1 = LED - 5mm [color="White (6500K)" package="5 mm [THT]"]
  Q1 = NPN-Transistor [part_number=BCU81 package="TO92 [THT]"]
  J2 = female pin header, 1 pin [form="♀ (female)"]  # not connected
  J3 = female pin header, 1 pin [form="♀ (female)"]  # not connected
  J4 = female pin header, 1 pin [form="♀ (female)"]  # not connected
  J5 = female pin header, 1 pin [form="♀ (female)"]  # not connected
  J6 = female pin header, 2 pins [form="♀ (female)"]  # not connected
  J7 = female pin header, 2 pins [form="♀ (female)"]  # not connected
  J8 = female pin header, 2 pins [form="♀ (female)"]  # not connected
  J9 = female pin header, 2 pins [form="♀ (female)"]  # not connected
  J10 = female pin header, 2 pins [form="♀ (female)"]  # not connected
  J11 = female pin header, 2 pins [form="♀ (female)"]  # not connected
  J12 = female pin header, 2 pins [form="♀ (female)"]  # not connected
  J13 = female pin header, 2 pins [form="♀ (female)"]  # not connected

nets:
  N1: R2.Pin_0, LED2.cathode
  N2: R2.Pin_1, R1.Pin_1, R3.Pin_1, Q1.C
  N3: R1.Pin_0, LED1.cathode
  N4: R3.Pin_0, LED3.cathode
  N5: R4.Pin_0, Q1.B
  N6: R4.Pin_1, J1.pin3
  N7: J1.pin1, Q1.E
  N8: J1.pin2, LED2.anode, LED3.anode, LED1.anode

notes:
  Single headers are 2mm holes for camera module attachment.
  Blocs of four header modules are 3mm holes for pan/tilt support attachment
  From top to bottom
  - Signal
  - +5V
  - GND
  Blue line is where to cut stripboard for camera module ribbon cable
