# Fritzing sketch PowerRail (saved by Fritzing 0.8.7b)
stripboards: 1

parts:
  C5 = Electrolytic Capacitor [capacitance=1mF voltage=16V package="100 mil [THT, electrolytic]"]
  ArduinoPower = female pin header, 2 pins [form="♀ (female)"]
  LightingPower = female pin header, 2 pins [form="♀ (female)"]
  TiltPower = female pin header, 2 pins [form="♀ (female)"]
  PanPower = female pin header, 2 pins [form="♀ (female)"]
  RaspiPower = female pin header, 2 pins [form="♀ (female)"]
  C3 = Electrolytic Capacitor [capacitance=1mF voltage=16V package="100 mil [THT, electrolytic]"]
  C1 = Electrolytic Capacitor [capacitance=1mF voltage=16V package="100 mil [THT, electrolytic]"]
  +5V = female pin header, 1 pin [form="♀ (female)"]
  GND = female pin header, 1 pin [form="♀ (female)"]
  TiltSignal = female pin header, 2 pins [form="♀ (female)"]
  PanSignal = female pin header, 2 pins [form="♀ (female)"]
  C2 = Electrolytic Capacitor [capacitance=1mF voltage=16V package="100 mil [THT, electrolytic]"]
  C4 = Electrolytic Capacitor [capacitance=1mF voltage=16V package="100 mil [THT, electrolytic]"]
  LightingSignal = female pin header, 2 pins [form="♀ (female)"]

nets:
  N1: C5.-, ArduinoPower.pin1, LightingPower.pin1, TiltPower.pin1, PanPower.pin1, RaspiPower.pin1, C3.-, C1.-, GND.pin1, C2.-, C4.-
  N2: C5.+, ArduinoPower.pin2, LightingPower.pin2, TiltPower.pin2, PanPower.pin2, RaspiPower.pin2, C3.+, C1.+, +5V.pin1, C2.+, C4.+
  N3: TiltSignal.pin1, TiltSignal.pin2
  N4: PanSignal.pin1, PanSignal.pin2
  N5: LightingSignal.pin1, LightingSignal.pin2

notes:
  GND on left
  + 5V on right
  Headers from top to bottom
  - Raspberry Pi power
  - Arduino power
  - Pan servo power
  - Tilt servo power
  - Camera module lighting power
  Signal wire for tilt servo
  Signal wire for pan servo
  Signal wire for camera lighting
