# Fritzing sketch RaspiDuinoRover (saved by Fritzing 0.8.7b)
perfboards: 1
stripboards: 1

parts:
  R2 = Resistor [tolerance=±5% resistance=220 package=THT]
  R1 = Resistor [tolerance=±5% resistance=220 package=THT]
  R3 = Resistor [tolerance=±5% resistance=220 package=THT]
  R4 = Resistor [tolerance=±5% resistance=360 package=THT]
  J1 = female pin header, 3 pins [form="♀ (female)"]
  LED2 = LED - 5mm [color="White (6500K)" package="5 mm [THT]"]
  LED3 = LED - 5mm [color="White (6500K)" package="5 mm [THT]"]
  LED1 = LED - 5mm [color="White (6500K)" package="5 mm [THT]"]
  Q1 = NPN-Transistor [part_number=BCU81 package="TO92 [THT]"]
  J2 = female pin header, 1 pin [form="♀ (female)"]  # not connected
  J3 = female pin header, 1 pin [form="♀ (female)"]  # not connected
  J4 = female pin header, 1 pin [form="♀ (female)"]  # not connected
  J5 = female pin header, 1 pin [form="♀ (female)"]  # not connected
  J6 = female pin header, 2 pins [form="♀ (female)"]  # not connected
  J7 = female pin header, 2 pins [form="♀ (female)"]  # not connected
  J8 = female pin header, 2 pins [form="♀ (female)"]  # not connected
  J9 = female pin header, 2 pins [form="♀ (female)"]  # not connected
  J10 = female pin header, 2 pins [form="♀ (female)"]  # not connected
  J11 = female pin header, 2 pins [form="♀ (female)"]  # not connected
  J12 = female pin header, 2 pins [form="♀ (female)"]  # not connected
  J13 = female pin header, 2 pins [form="♀ (female)"]  # not connected
  GND1 = female pin header, 1 pin [form="♀ (female)"]
  +5V1 = female pin header, 1 pin [form="♀ (female)"]
  TiltSignal1 = female pin header, 2 pins [form="♀ (female)"]
  PanSignal1 = female pin header, 2 pins [form="♀ (female)"]
  C6 = Electrolytic Capacitor [capacitance=1mF voltage=16V package="100 mil [THT, electrolytic]"]
  C7 = Electrolytic Capacitor [capacitance=1mF voltage=16V package="100 mil [THT, electrolytic]"]
  C8 = Electrolytic Capacitor [capacitance=1mF voltage=16V package="100 mil [THT, electrolytic]"]
  C9 = Electrolytic Capacitor [capacitance=1mF voltage=16V package="100 mil [THT, electrolytic]"]
  C10 = Electrolytic Capacitor [capacitance=1mF voltage=16V package="100 mil [THT, electrolytic]"]
  RaspiPower1 = female pin header, 2 pins [form="♀ (female)"]
  PanPower1 = female pin header, 2 pins [form="♀ (female)"]
  TiltPower1 = female pin header, 2 pins [form="♀ (female)"]
  LightingPower1 = female pin header, 2 pins [form="♀ (female)"]
  ArduinoPower1 = female pin header, 2 pins [form="♀ (female)"]
  Part1 = Arduino Motor Shield (Rev3)
  RaspberryPi1 = Raspberry Pi Model B
  TiltServo = Basic Servo
  PanServo = Basic Servo
  LightingSignal1 = female pin header, 2 pins [form="♀ (female)"]

nets:
  N1: R2.Pin_0, LED2.cathode
  N2: R2.Pin_1, R1.Pin_1, R3.Pin_1, Q1.C
  N3: R1.Pin_0, LED1.cathode
  N4: R3.Pin_0, LED3.cathode
  N5: R4.Pin_0, Q1.B
  lighting signal: R4.Pin_1, J1.pin3, Part1.D6_PWM, LightingSignal1.pin1, LightingSignal1.pin2
  GND: J1.pin1, Q1.E, GND1.pin1, C6.-, C7.-, C8.-, C9.-, C10.-, RaspiPower1.pin1, PanPower1.pin1, TiltPower1.pin1, LightingPower1.pin1, ArduinoPower1.pin1, Part1.GND, RaspberryPi1.GND, TiltServo.gnd, PanServo.gnd
  +5V: J1.pin2, LED2.anode, LED3.anode, LED1.anode, +5V1.pin1, C6.+, C7.+, C8.+, C9.+, C10.+, RaspiPower1.pin2, PanPower1.pin2, TiltPower1.pin2, LightingPower1.pin2, ArduinoPower1.pin2, Part1.5V, RaspberryPi1.5V, TiltServo.vcc, PanServo.vcc
  tilt signal: TiltSignal1.pin1, TiltSignal1.pin2, Part1.D5_PWM, PanServo.pulse
  pan signal: PanSignal1.pin1, PanSignal1.pin2, Part1.D4, TiltServo.pulse
  N6: Part1.SDA, RaspberryPi1.SDA
  N7: Part1.SCL, RaspberryPi1.SCL

notes:
  +5V input
  Camera module lighting.
  See "CameraLighting.fzz"
  Common power rail.
  See "PowerRail.fzz"

custom parts:
  Raspberry Pi Model B: Raspberry Pi (Model B)
