# Fritzing sketch battery_power_board (saved by Fritzing 0.8.7b)
perfboards: 1

parts:
  J1 = single row smd female pin header, 1 pin [form="♀ (female)"]  # not connected
  J2 = single row smd female pin header, 1 pin [form="♀ (female)"]  # not connected
  J3 = single row smd female pin header, 1 pin [form="♀ (female)"]  # not connected
  J4 = single row smd female pin header, 1 pin [form="♀ (female)"]  # not connected
  From_PB = screw terminal, 3 pins
  To_MS = screw terminal, 3 pins
  To_CPR = screw terminal, 3 pins
  LED1 = LED - 5mm [color="Yellow (595nm)" package="5 mm [THT]"]
  R1 = Resistor [tolerance=±5% resistance=220 package=THT]
  S7V8A = single row smd female pin header, 4 pins [form="♀ (female)"]

nets:
  N1: From_PB.pin1, To_CPR.pin3, LED1.anode, S7V8A.pin2
  N2: From_PB.pin3, To_MS.pin3, To_CPR.pin1, R1.Pin_0, S7V8A.pin3
  N3: To_MS.pin1, S7V8A.pin4
  N4: LED1.cathode, R1.Pin_1

notes:
  +5V IN
  +5V OUT
  +8V OUT
  Notes :
  - 4 contacts header is where to put Pololu S7V8A DC-DC converter
  - from top to down
  - SHDN (floating or HIGH to enable converter)
  - VIN
  - GND
  - VOUT
  - single headers are where to drill 3mm holes to fix the board
